# Fritzing sketch ArduinoSenderCircuitBoard (saved by Fritzing 0.7.10b)
breadboards: 1

parts:
  R1 = Resistor [tolerance=±5% resistance=22k package=THT]
  Arduino1 = Arduino
  R2 = Resistor [tolerance=±5% resistance=15k package=THT]
  U1 = mystery part, 5 pins [chip_label=RF901SM]

nets:
  N1: R1.Pin_0, Arduino1.D7
  N2: R1.Pin_1, U1.pin3
  N3: Arduino1.GND, R2.Pin_1, U1.pin2, U1.pin4
  N4: Arduino1.D8, U1.pin5

notes:
  black= ground, red= +12V, need on/off switch
  Pin 7 is used to detect
  that 12V power is switched on.
  R1 and R2 form voltage divider: 15kOhm/(15kOhm+ 22kOhm)* 12V= 4.86V
  Pin 8 sends actual signal to RF901SM.
